# Fritzing sketch Driver (saved by Fritzing 0.9.1b)
breadboards: 1

parts:
  IC1 = L293D [package=THT]
  IC2 = L293D [package=THT]
  IC3 = L293D [package=THT]
  M1 = Stepper Motor - Bipolar
  M2 = Stepper Motor - Bipolar
  M3 = Stepper Motor - Bipolar
  Power_plug1 = Power plug
  IC4 = Voltage Regulator [package=78xxl]
  C1 = Capacitor [package=cap-pth-small2]
  C2 = Capacitor [package=cap-pth-small2]

nets:
  N1: IC1.Enable_1, IC1.Enable_2, IC1.+V, IC2.Enable_1, IC2.Enable_2, IC2.+V, IC3.+V, IC4.OUT, C2.1
  N2: IC1.Out_1_(_Controlled_by_Enable_1_), M1.A
  GND: IC1.0V, IC2.0V, IC3.0V, Power_plug1.GND, IC4.GND, C1.1, C2.2
  N3: IC1.Out_2_(_Controlled_by_Enable_1_), M1.B
  N4: IC1.Out_3_(_Controlled_by_Enable_2_), M1.D
  N5: IC1.Out_4_(_Controlled_by_Enable_2_), M1.C
  N6: IC2.Out_1_(_Controlled_by_Enable_1_), M2.A
  N7: IC2.Out_2_(_Controlled_by_Enable_1_), M2.B
  N8: IC2.Out_3_(_Controlled_by_Enable_2_), M2.C
  N9: IC2.Out_4_(_Controlled_by_Enable_2_), M2.D
  N10: IC3.Enable_1, IC3.Enable_2
  N11: IC3.Out_1_(_Controlled_by_Enable_1_), M3.A
  N12: IC3.Out_2_(_Controlled_by_Enable_1_), M3.B
  N13: IC3.Out_3_(_Controlled_by_Enable_2_), M3.C
  N14: IC3.Out_4_(_Controlled_by_Enable_2_), M3.D
  N15: Power_plug1.VCC, IC4.IN, C1.2
